# Fritzing sketch blaster (saved by Fritzing 0.9.3b)
circuit board: 8.46667cm x 5.64444cm
breadboards: 1

parts:
  R1 = Resistor [tolerance=±5% resistance=10k package=THT]
  R2 = Resistor [tolerance=±5% resistance=330 package=THT]
  U1 = attiny85 [package=dip]
  JP4 = Header 6 [package=1x06-smd]
  JP5 = Header 6 [package=1x06-smd]

nets:
  N1: R1.Pin_0, U1.Pin_4, JP4.6, JP5.1
  N2: R1.Pin_1, U1.Pin_5, JP5.5
  N3: R2.Pin_0, JP4.5
  N4: R2.Pin_1, U1.Pin_6
  N5: U1.Pin_8, JP4.4, JP5.2, JP5.4
